// Logisim project Relogio.circ as structural Verilog: 1 circuit, main circuit main
module main (
  input  [7:0] in_1,
  input  [7:0] in_2,
  input  [7:0] in_3,
  input  [7:0] in_4,
  input  in_5
);

  wire and_1_out, and_2_out, and_3_out, and_4_out, clock_1_out, decodificador_1_p5, decodificador_1_p6,
       decodificador_1_p7, decodificador_1_p8, decodificador_1_p9, decodificador_1_p10, decodificador_1_p11,
       decodificador_2_p5, decodificador_2_p6, decodificador_2_p7, decodificador_2_p8, decodificador_2_p9,
       decodificador_2_p10, decodificador_2_p11, decodificador_3_p5, decodificador_3_p6, decodificador_3_p7,
       decodificador_3_p8, decodificador_3_p9, decodificador_3_p10, decodificador_3_p11, decodificador_4_p5,
       decodificador_4_p6, decodificador_4_p7, decodificador_4_p8, decodificador_4_p9, decodificador_4_p10,
       decodificador_4_p11, main_1_p2, main_1_p3, main_1_p4, main_1_p5, main_1_p6, main_2_p2, main_2_p3,
       main_2_p4, main_2_p5, main_2_p6, main_3_p2, main_3_p3, main_3_p4, main_3_p5, main_3_p6, main_4_p3,
       main_4_p4, main_4_p5, main_4_p6, or_1_out, or_3_out, or_4_out, or_6_out, or_8_out;

  Register register_1 (.D(in_1));  // open: en, Q, clk, clr
  or or_1 (or_1_out, and_1_out, in_5);
  // FlipFlopJK_zero_a_dez_main main_1: pin names not known; wires that end beside it: or_1_out, main_1_p2, main_1_p3, main_1_p4, main_1_p5, main_1_p6
  and and_1 (and_1_out, main_1_p5, main_2_p4);
  buf or_2 (main_1_p2, or_3_out);  // OR_Gate
  // Decodificador decodificador_1: pin names not known; wires that end beside it: main_1_p3, main_1_p4, main_1_p5, main_1_p6, decodificador_1_p5, decodificador_1_p6, decodificador_1_p7, decodificador_1_p8, decodificador_1_p9, decodificador_1_p10, decodificador_1_p11
  or or_3 (or_3_out, and_2_out, and_1_out);
  _7_Segment_Display u_7_segment_display_1 (
    .g(decodificador_1_p11), .f(decodificador_1_p10), .a(decodificador_1_p5), .b(decodificador_1_p6),
    .e(decodificador_1_p9), .d(decodificador_1_p8), .c(decodificador_1_p7));  // open: dp
  Register register_2 (.D(in_2));  // open: en, Q, clk, clr
  and and_2 (and_2_out, main_2_p5, main_2_p3);
  or or_4 (or_4_out, or_3_out, in_5);
  // FlipFlopJK_zero_a_dez_main main_2: pin names not known; wires that end beside it: or_4_out, main_2_p2, main_2_p3, main_2_p4, main_2_p5, main_2_p6
  // Decodificador decodificador_2: pin names not known; wires that end beside it: main_2_p3, main_2_p4, main_2_p5, main_2_p6, decodificador_2_p5, decodificador_2_p6, decodificador_2_p7, decodificador_2_p8, decodificador_2_p9, decodificador_2_p10, decodificador_2_p11
  _7_Segment_Display u_7_segment_display_2 (
    .g(decodificador_2_p11), .f(decodificador_2_p10), .a(decodificador_2_p5), .b(decodificador_2_p6),
    .e(decodificador_2_p9), .d(decodificador_2_p8), .c(decodificador_2_p7));  // open: dp
  Register register_3 (.D(in_3));  // open: en, Q, clk, clr
  or or_5 (main_2_p2, and_3_out, and_1_out);
  or or_6 (or_6_out, main_2_p2, in_5);
  // FlipFlopJK_zero_a_dez_main main_3: pin names not known; wires that end beside it: or_6_out, main_3_p2, main_3_p3, main_3_p4, main_3_p5, main_3_p6
  and and_3 (and_3_out, main_3_p5, main_3_p4);
  // Decodificador decodificador_3: pin names not known; wires that end beside it: main_3_p3, main_3_p4, main_3_p5, main_3_p6, decodificador_3_p5, decodificador_3_p6, decodificador_3_p7, decodificador_3_p8, decodificador_3_p9, decodificador_3_p10, decodificador_3_p11
  or or_7 (main_3_p2, and_1_out, and_4_out);
  _7_Segment_Display u_7_segment_display_3 (
    .g(decodificador_3_p11), .f(decodificador_3_p10), .a(decodificador_3_p5), .b(decodificador_3_p6),
    .e(decodificador_3_p9), .d(decodificador_3_p8), .c(decodificador_3_p7));  // open: dp
  Register register_4 (.D(in_4));  // open: en, Q, clk, clr
  and and_4 (and_4_out, main_4_p5, main_4_p3);
  or or_8 (or_8_out, main_3_p2, in_5);
  Clock clock_1 (.out(clock_1_out));
  // FlipFlopJK_zero_a_dez_main main_4: pin names not known; wires that end beside it: or_8_out, clock_1_out, main_4_p3, main_4_p4, main_4_p5, main_4_p6
  // Decodificador decodificador_4: pin names not known; wires that end beside it: main_4_p3, main_4_p4, main_4_p5, main_4_p6, decodificador_4_p5, decodificador_4_p6, decodificador_4_p7, decodificador_4_p8, decodificador_4_p9, decodificador_4_p10, decodificador_4_p11
  _7_Segment_Display u_7_segment_display_4 (
    .g(decodificador_4_p11), .f(decodificador_4_p10), .a(decodificador_4_p5), .b(decodificador_4_p6),
    .e(decodificador_4_p9), .d(decodificador_4_p8), .c(decodificador_4_p7));  // open: dp
endmodule
